# Fritzing sketch ControladorLEDsCocina_SSR (saved by Fritzing 0.9.3b)
breadboards: 1

parts:
  WeMos_D1_Mini1 = WeMos D1 Mini
  12Vcc_->_5Vcc = RioRand LM2596
  Strip1 = Screw terminal - 2 pins [package=THT]
  Relay1 = Screw terminal - 2 pins [package=THT]
  Strip2 = Screw terminal - 2 pins [package=THT]
  Strip3 = Screw terminal - 2 pins [package=THT]
  Strip4 = Screw terminal - 2 pins [package=THT]
  Relay2 = Screw terminal - 2 pins [package=THT]
  Relay3 = Screw terminal - 2 pins [package=THT]
  Relay4 = Screw terminal - 2 pins [package=THT]
  5Vcc = Screw terminal - 2 pins [package=THT]
  CH1_|_CH2 = Screw terminal - 2 pins [package=THT]
  CH3_|_CH4 = Screw terminal - 2 pins [package=THT]
  PIR = Screw terminal - 2 pins [package=THT]
  12Vcc = screw terminal, 2 pins
  Header_Cont_5V = female pin header, 2 pins [form="♀ (female)"]

nets:
  N1: WeMos_D1_Mini1.5V, 5Vcc.pin1, Header_Cont_5V.pin2
  N2: WeMos_D1_Mini1.D0, PIR.pin2
  N3: WeMos_D1_Mini1.D5, CH3_|_CH4.pin1
  N4: WeMos_D1_Mini1.D6, CH3_|_CH4.pin2
  N5: WeMos_D1_Mini1.D7, CH1_|_CH2.pin1
  N6: WeMos_D1_Mini1.D8, CH1_|_CH2.pin2
  N7: WeMos_D1_Mini1.G, 12Vcc_->_5Vcc.Pin_4, 5Vcc.pin2
  N8: 12Vcc_->_5Vcc.Pin_1, Strip1.pin1, Strip2.pin1, Strip3.pin1, Strip4.pin1, 12Vcc.pin2
  N9: 12Vcc_->_5Vcc.Pin_2, Relay1.pin1, Relay2.pin1, Relay3.pin1, Relay4.pin1, 12Vcc.pin1
  N10: 12Vcc_->_5Vcc.Pin_3, Header_Cont_5V.pin1
  N11: Strip1.pin2, Relay1.pin2
  N12: Strip2.pin2, Relay2.pin2
  N13: Strip3.pin2, Relay3.pin2
  N14: Strip4.pin2, Relay4.pin2
